# Fritzing sketch rc_lights_controller (saved by Fritzing 0.9.2b)
breadboards: 1

parts:
  U1 = attiny85 [package=dip]
  Q3 = NPN-Transistor [part_number=BC337-40 package="TO92 [THT]"]
  R1 = Resistor [tolerance=±5% resistance=470 package=THT]
  Q4 = NPN-Transistor [part_number=BC337-40 package="TO92 [THT]"]
  Q5 = NPN-Transistor [part_number=BC337-40 package="TO92 [THT]"]
  R2 = Resistor [tolerance=±5% resistance=470 package=THT]
  R3 = Resistor [tolerance=±5% resistance=470 package=THT]

nets:
  N1: U1.Pin_1, R1.Pin_1
  N2: U1.Pin_2, R2.Pin_1
  N3: U1.Pin_3, R3.Pin_1
  N4: U1.Pin_4, Q3.E, Q4.E, Q5.E
  N5: Q3.B, R1.Pin_0
  N6: Q4.B, R2.Pin_0
  N7: Q5.B, R3.Pin_0
